# Fritzing sketch arduino-sketch (saved by Fritzing 0.9.2b)

parts:
  Bauteil1 = Arduino Uno (Rev3)
  DHT1 = DHT11 Humitidy and Temperature Sensor
  R1 = Resistor [tolerance=±5% resistance=10k package=THT]

nets:
  N1: Bauteil1.D2, DHT1.DATA, R1.Pin_1
  5V: Bauteil1.5V, DHT1.VDD, R1.Pin_0
  GND: Bauteil1.GND, DHT1.GND

notes:
  PullBack-Resistor

custom parts:
  DHT11 Humitidy and Temperature Sensor: DHT11 Humidity and Temperature Sensor
