# Fritzing sketch raspberry-sketch (saved by Fritzing 0.9.2b)

parts:
  RaspberryPi1 = Raspberry Pi Model B
  Bauteil1 = ITEAD PN532 NFC Module

nets:
  5V: RaspberryPi1.5V, Bauteil1.5V
  GND: RaspberryPi1.GND, RaspberryPi1.TXD, Bauteil1.GND
  N1: RaspberryPi1.MISO, Bauteil1.NSS, Bauteil1.MISO

custom parts:
  Raspberry Pi Model B: Raspberry Pi (Model B)
  ITEAD PN532 NFC Module: Breakout board Platform Based On Arduino by Iteadstudio Principal features : Electronic Brick Ports 3.3V or 5V power supply The official support forum: support@iteadstudio.com
